# Fritzing sketch NanoLedPushbutton (saved by Fritzing 0.9.4)
breadboards: 1

parts:
  S1 = Pushbutton [package="[THT]"]
  LED1 = LED - 5mm [color="Red (633nm)" package="5 mm [THT]"]
  Part1 = Arduino Nano (Rev3.0)

nets:
  N1: S1.Pin_1, S1.Pin_2, Part1.D2
  GND: S1.Pin_3, S1.Pin_4, LED1.cathode, Part1.GND
  N2: LED1.anode, Part1.D3
